// Logisim project Circuito Aula 1 - 241037112 Pedro Henrique Dias Avelar.circ as structural Verilog: 1 circuit, main circuit main
module main (
);

  wire and_1_out, and_2_out, and_3_out, and_4_out, and_5_out, and_6_out, and_7_out, and_8_out, and_9_out,
       and_10_out, nand_1_out, nand_2_out, nand_3_out, nand_4_out, nand_5_out, nand_6_out, nand_7_out,
       nand_8_out, nand_9_out, nand_10_out, nand_11_out, nand_12_out, nand_13_out, nand_14_out, nand_15_out,
       nand_16_out, nand_17_out, nand_18_out, nand_19_out, nand_20_out, nand_21_out, nand_22_out,
       nand_23_out, nand_24_out, nand_25_out, nand_26_out, nand_27_out, nand_28_out, nand_29_out,
       nand_30_out, nand_31_out, nand_32_out, nand_33_out, nand_34_out, nand_35_out, nand_36_out,
       nand_37_out, nand_38_out, nand_39_out, nand_40_out, nand_41_out, nand_42_out, nand_43_out,
       nand_44_out, nand_45_out, nand_46_out, nand_47_out, nand_48_out, nand_49_out, nand_50_out,
       nand_51_out, nand_52_out, nand_53_out, nand_54_out, nand_55_out, nand_56_out, nand_57_out,
       nand_58_out, nand_59_out, nand_60_out, nand_61_out, nand_62_out, nand_63_out, not_1_out, not_2_out,
       not_3_out, not_4_out, not_5_out, not_6_out, not_7_out, not_8_out, not_9_out, not_10_out, not_11_out,
       or_1_out, or_2_out, or_3_out, or_4_out, or_5_out, or_6_out;

  not not_1 (not_1_out, 1'b1);
  not not_2 (not_2_out, 1'b1);
  not not_3 (not_3_out, 1'b1);
  not not_4 (not_4_out, 1'b1);
  not not_5 (not_5_out, 1'b1);
  not not_6 (not_6_out, 1'b1);
  not not_7 (not_7_out, or_1_out);
  or or_1 (or_1_out, not_1_out, not_2_out);
  and and_1 (and_1_out, 1'b1, 1'b1);
  and and_2 (and_2_out, 1'b1, 1'b1, 1'b1);
  and and_3 (and_3_out, 1'b1, 1'b1);
  and and_4 (and_4_out, 1'b1, 1'b1);
  and and_5 (and_5_out, not_3_out, not_4_out);
  and and_6 (and_6_out, not_5_out, 1'b1);
  and and_7 (and_7_out, 1'b1, not_6_out);
  nand nand_1 (nand_1_out, 1'b1, 1'b1);
  nand nand_2 (nand_2_out, 1'b1, 1'b1);
  nand nand_3 (nand_3_out, 1'b1, 1'b1);
  nand nand_4 (nand_4_out, 1'b1, 1'b1);
  nand nand_5 (nand_5_out, 1'b1, 1'b1);
  // Probe on not_7_out
  or or_2 (or_2_out, and_1_out, and_2_out);
  nand nand_6 (nand_6_out, 1'b1, 1'b0);
  nand nand_7 (nand_7_out, 1'b1, 1'b0);
  nand nand_8 (nand_8_out, 1'b0, 1'b0);
  nand nand_9 (nand_9_out, nand_1_out, nand_1_out);
  nand nand_10 (nand_10_out, nand_2_out, nand_3_out);
  or or_3 (or_3_out, and_4_out, and_5_out);
  not not_8 (not_8_out, 1'b1);
  or or_4 (or_4_out, and_6_out, and_7_out);
  nand nand_11 (nand_11_out, nand_6_out, nand_7_out);
  nand nand_12 (nand_12_out, nand_9_out, nand_9_out);
  nand nand_13 (nand_13_out, 1'b1, 1'b1);
  nand nand_14 (nand_14_out, 1'b1, nand_4_out);
  nand nand_15 (nand_15_out, nand_5_out, 1'b0);
  nand nand_16 (nand_16_out, 1'b1, 1'b0);
  nand nand_17 (nand_17_out, 1'b1, 1'b1);
  nand nand_18 (nand_18_out, 1'b1, 1'b0);
  or or_5 (or_5_out, or_2_out, and_3_out);
  // Probe on or_5_out
  and and_8 (and_8_out, 1'b1, or_3_out);
  and and_9 (and_9_out, not_8_out, or_4_out);
  nand nand_19 (nand_19_out, nand_11_out, nand_11_out);
  nand nand_20 (nand_20_out, nand_10_out, nand_10_out);
  nand nand_21 (nand_21_out, nand_13_out, 1'b1);
  nand nand_22 (nand_22_out, nand_14_out, nand_14_out);
  nand nand_23 (nand_23_out, nand_15_out, nand_16_out);
  not not_9 (not_9_out, 1'b1);
  not not_10 (not_10_out, 1'b1);
  nand nand_24 (nand_24_out, nand_19_out, nand_8_out);
  nand nand_25 (nand_25_out, nand_20_out, nand_20_out);
  nand nand_26 (nand_26_out, nand_21_out, nand_21_out);
  nand nand_27 (nand_27_out, nand_22_out, nand_22_out);
  nand nand_28 (nand_28_out, nand_17_out, 1'b0);
  and and_10 (and_10_out, not_9_out, not_10_out);
  or or_6 (or_6_out, and_8_out, and_9_out);
  // Probe on or_6_out
  nand nand_29 (nand_29_out, nand_12_out, nand_25_out);
  nand nand_30 (nand_30_out, nand_26_out, nand_26_out);
  nand nand_31 (nand_31_out, 1'b0, nand_23_out);
  nand nand_32 (nand_32_out, nand_28_out, nand_18_out);
  nand nand_33 (nand_33_out, nand_32_out, 1'b0);
  not not_11 (not_11_out, and_10_out);
  nand nand_34 (nand_34_out, 1'b1, nand_29_out);
  nand nand_35 (nand_35_out, 1'b1, 1'b1);
  nand nand_36 (nand_36_out, nand_30_out, nand_27_out);
  // Probe on not_11_out
  nand nand_37 (nand_37_out, nand_34_out, nand_34_out);
  nand nand_38 (nand_38_out, nand_35_out, nand_36_out);
  nand nand_39 (nand_39_out, nand_31_out, nand_33_out);
  nand nand_40 (nand_40_out, nand_38_out, nand_38_out);
  nand nand_41 (nand_41_out, nand_37_out, nand_37_out);
  nand nand_42 (nand_42_out, nand_40_out, nand_40_out);
  nand nand_43 (nand_43_out, nand_41_out, nand_42_out);
  nand nand_44 (nand_44_out, 1'b1, 1'b1);
  nand nand_45 (nand_45_out, 1'b1, 1'b1);
  nand nand_46 (nand_46_out, 1'b1, 1'b1);
  nand nand_47 (nand_47_out, 1'b1, 1'b1);
  nand nand_48 (nand_48_out, 1'b1, 1'b1);
  nand nand_49 (nand_49_out, 1'b1, 1'b1);
  nand nand_50 (nand_50_out, 1'b1, 1'b1);
  // Probe on nand_50_out
  nand nand_51 (nand_51_out, 1'b1, 1'b1);
  nand nand_52 (nand_52_out, nand_45_out, nand_46_out);
  // Probe on nand_52_out
  nand nand_53 (nand_53_out, nand_47_out, nand_48_out);
  nand nand_54 (nand_54_out, 1'b1, 1'b1);
  nand nand_55 (nand_55_out, 1'b1, nand_49_out);
  // Probe on nand_56_out
  nand nand_56 (nand_56_out, nand_51_out, nand_51_out);
  nand nand_57 (nand_57_out, nand_44_out, nand_53_out);
  nand nand_58 (nand_58_out, nand_54_out, 1'b1);
  nand nand_59 (nand_59_out, nand_58_out, nand_55_out);
  nand nand_60 (nand_60_out, 1'b1, nand_57_out);
  nand nand_61 (nand_61_out, 1'b1, 1'b1);
  nand nand_62 (nand_62_out, nand_61_out, nand_59_out);
  nand nand_63 (nand_63_out, nand_60_out, nand_62_out);

  // Notes on the sheet:
  //   1.A
  //   X
  //   Y
  //   2.A
  //   A
  //   B
  //   C
  //   A
  //   2B
  //   B
  //   C
  //   3.A
  //   B
  //   C
  //   3.B
  //   A
  //   B
  //   C
  //   4
  //   S0
  //   S1
  //   D0
  //   D1
  //   D2
  //   D3
  //   X*Y=!(!X+!Y)
  //   A
  //   B*C
  //   BC+!B!C
  //   !BC+B!C
  //   !B*!C
  //   D2*!S0
  //   X
  //   Y
  //   B*!C
  //   (D2*!S0)+(D3*S0)
  //   D3*S0
  //   D1*S0
  //   1.B
  //   X+Y=!(!X*!Y)
  //   A(BC+!B!C)
  //   !A(!BC+B!C)
  //   !B*C
  //   D0*!S0
  //   C-OUT
  //   (B*C)+(!B*!C)
  //   (D0*!S0)+(D1*S0)
  //   (!B*C)+(B+!C)
  //   S1*((D2*!S0)+(D3*S0))
  //   A*((B*C)+(!B*!C)
  //   S1*((D0*!S0)+(D1*S0))
  //   !A*((!B*C)+(B*!C)
  //   Y
  //   3.B
  //   A
  //   B
  //   C
  //   X
  //   Y
  //   X
  //   Y
  //   B*C
  //   Retirando as NANDs redundantes
  //   !B*!C
  //   B*!C
  //   !B*C
  //   (B*C)+(!B*!C)
  //   (!B*C)+(B+!C)
  //   A*((B*C)+(!B*!C)
  //   !A*((!B*C)+(B*!C)
endmodule
