// Logisim project Modelo Q01.circ as structural Verilog: 1 circuit, main circuit main
module main (
  input  C,
  input  [1:0] AB,
  output X,
  output Y
);

  wire not_1_out;

  not not_1 (not_1_out, C);
  Multiplexer #(.select(2), .enable("false")) multiplexer_1 (
    .in0(1'b0), .in1(C), .in2(not_1_out), .in3(1'b1), .out(X), .sel(AB));
  Multiplexer #(.select(2), .enable("false")) multiplexer_2 (
    .in0(1'b1), .in1(not_1_out), .in2(1'b0), .in3(C), .out(Y), .sel(AB));
endmodule
