// Logisim project Modelo Q02.circ as structural Verilog: 1 circuit, main circuit main
module main (
  input  [2:0] EFG,
  input  [3:0] ABCD,
  output Z
);

  wire D10_D11_out, D15_D0_out, D15_D9_out, decoder_1_out0, decoder_1_out7, decoder_1_out9, decoder_1_out10,
       decoder_1_out11, decoder_1_out15;

  Decoder #(.select(4), .enable("false")) decoder_1 (
    .out0(decoder_1_out0), .out7(decoder_1_out7), .out9(decoder_1_out9), .out10(decoder_1_out10),
    .out11(decoder_1_out11), .out15(decoder_1_out15), .sel(ABCD));  // open: out1, out2, out3, out4, out5, out6, out8, out12, out13, out14
  or D15_D0 (D15_D0_out, decoder_1_out0, decoder_1_out15);
  or D10_D11 (D10_D11_out, decoder_1_out10, decoder_1_out11);
  or D15_D9 (D15_D9_out, decoder_1_out15, decoder_1_out9);
  Multiplexer #(.select(3), .enable("false")) multiplexer_1 (
    .in0(1'b0), .in1(D15_D0_out), .in2(decoder_1_out7), .in3(1'b1), .in4(D15_D9_out), .in5(1'b0),
    .in6(D10_D11_out), .in7(1'b1), .out(Z), .sel(EFG));
endmodule
